# Fritzing sketch Arduino_Uno_i2C_LCD V_3 (saved by Fritzing 0.9.3b)
circuit board: 8.46667cm x 5.64444cm
breadboards: 1

parts:
  LCD1 = LCD screen
  LCM1602_IIC1 = LCM1602 IIC [part_number="LCM1602 IIC" chip_label="LCM1602 IIC" package="DIP (Dual Inline) [THT]"]
  LED1 = LED - 3mm [color="White (8000K)" package="3 mm [THT]"]
  R6 = Resistor [tolerance=±5% resistance=560 package=THT]
  R4 = Resistor [tolerance=±5% resistance=4.7k package=THT]
  S2 = Pushbutton [package="[THT]"]
  S6 = Pushbutton [package="[THT]"]
  S7 = Pushbutton [package="[THT]"]
  S4 = Pushbutton [package="[THT]"]
  R7 = Resistor [tolerance=±5% resistance=220 package=THT]
  R3 = Resistor [tolerance=±5% resistance=10k package=THT]
  S3 = Pushbutton [package="[THT]"]
  R29 = Resistor [tolerance=±5% resistance=1k package=THT]
  S5 = Pushbutton [package="[THT]"]
  S15 = Pushbutton [package="[THT]"]
  R2 = Resistor [tolerance=±5% resistance=1M package=THT]
  R25 = Resistor [tolerance=±5% resistance=10k package=THT]
  Onderdeel1 = Arduino Uno (Rev3)
  R31 = Resistor [tolerance=±5% resistance=10k package=THT]
  S1 = Pushbutton [package="[THT]"]
  J1 = Piezo Speaker
  R30 = Resistor [tolerance=±5% resistance=100 package=THT]
  R32 = Resistor [tolerance=±5% resistance=10k package=THT]

nets (from the breadboard view):
  VSS: LCD1.VSS, LCM1602_IIC1.VSS
  VDD: LCD1.VDD, LCM1602_IIC1.VDD
  N1: LCD1.V0, LCM1602_IIC1.V0
  N2: LCD1.RS, LCM1602_IIC1.RS
  N3: LCD1.R/W, LCM1602_IIC1.RW
  N4: LCD1.E, LCM1602_IIC1.E
  N5: LCD1.DB0, LCM1602_IIC1.D0
  N6: LCD1.DB1, LCM1602_IIC1.D1
  N7: LCD1.DB2, LCM1602_IIC1.D2
  N8: LCD1.DB3, LCM1602_IIC1.D3
  N9: LCD1.DB4, LCM1602_IIC1.D4
  N10: LCD1.DB5, LCM1602_IIC1.D5
  N11: LCD1.DB6, LCM1602_IIC1.D6
  N12: LCD1.DB7, LCM1602_IIC1.D7
  N13: LCD1.LED+, LCM1602_IIC1.A
  N14: LCD1.LED-, LCM1602_IIC1.K
  GND: LCM1602_IIC1.GND, R3.Pin_1, R25.Pin_0, Onderdeel1.GND, R30.Pin_0, R32.Pin_0
  VCC: LCM1602_IIC1.VCC, R6.Pin_0, R4.Pin_0, R7.Pin_0, R29.Pin_0, S15.Pin_3, S15.Pin_4, R2.Pin_0, Onderdeel1.5V, R31.Pin_0, S1.Pin_3, S1.Pin_4
  N15: LCM1602_IIC1.SDA, Onderdeel1.A4/SDA
  N16: LCM1602_IIC1.SCL, Onderdeel1.A5/SCL
  N17: LCM1602_IIC1.LED_A, LCM1602_IIC1.LED_B
  N18: LED1.cathode, R3.Pin_0
  N19: LED1.anode, Onderdeel1.D6_PWM
  N20: R6.Pin_1, S4.Pin_3, S4.Pin_4
  N21: R4.Pin_1, S5.Pin_3, S5.Pin_4
  N22: S2.Pin_1, S2.Pin_2, S6.Pin_1, S6.Pin_2, S7.Pin_1, S7.Pin_2, S4.Pin_1, S4.Pin_2, S3.Pin_1, S3.Pin_2, S5.Pin_1, S5.Pin_2, S15.Pin_1, S15.Pin_2, R25.Pin_1, Onderdeel1.A0
  N23: S2.Pin_3, S2.Pin_4, R7.Pin_1
  N24: S6.Pin_3, S6.Pin_4, R31.Pin_1
  N25: S7.Pin_3, S7.Pin_4, R29.Pin_1
  N26: S3.Pin_3, S3.Pin_4, R2.Pin_1
  N27: Onderdeel1.D8, J1.pin2
  N28: Onderdeel1.D7, S1.Pin_1, S1.Pin_2, R32.Pin_1
  N29: J1.pin1, R30.Pin_1

custom parts:
  LCM1602 IIC: I2C-Module to use a 1602 or 2004 LCD on with the wire.h libory Serial LCD Modul

// code stored in the sketch: AnalogReadSerial2LCD_LED.ino
#include <Wire.h>
#include <LiquidCrystal_I2C.h>
LiquidCrystal_I2C lcd(0x27,2,1,0,4,5,6,7,3,POSITIVE);
#include "pitches.h"

const byte LCDswitchPin = 7;//variavel para o pin do butao lcd
byte LCDswitchState = 0; // variavel para ligar desligar lcd
byte prevLCDswitchState = 0;
byte LED = 6;
byte counter = 0; //contador para vezes de carregar no buttao
byte LCDswitchCounter = 0;   //variavel para contar a posição menu aumenta quando carregado

// butoes de musica define os valores de frequencias
short notes[] = {262, 294, 330, 349, 392, 440, 494}; // notas C, D, E, F, G, A, B

//////////////////////////////////////////////
void setup() {
  
  Serial.begin(9600);
  
  lcd.begin(16, 2);
  pinMode(LCDswitchPin, INPUT);
  pinMode(LED, OUTPUT);
  digitalWrite(LED, LOW); // o lcd fica desligado enquando esta em modo piano
  lcd.noBacklight();
} //fim setup

//////////////////////////////////////////////
void loop() {
  
  LCDswitchState = digitalRead(LCDswitchPin);
  short keyVal = analogRead(A0);
  Serial.println(keyVal);
  lcd.noDisplay();
  digitalWrite(LED, LOW); // o led do menu desligase sempre que chega ao fim
 
// ************** começa "LCDstart" quando carrega no butao menu ***********

    if (LCDswitchState == HIGH)  {
      digitalWrite(LED, HIGH); //led liga-se quando se entra no menu para se saber que esta no modo menu e o piano off
      lcd.display();
      lcd.clear();
      LCDstart();
      }
   
// ***********************************************************************

////// teclado piano e frequencias //////
// 220 ohm = C5 // 560 ohm = D5 // 1K ohm = E5 // etc...
  if(keyVal == 1023)  {
    tone(8, notes[0]); // do
    } // end if
    
        else if(keyVal >= 990 & keyVal <=1010)  {
          tone(8, notes[1]); // re
          } // end else if
    
        else if(keyVal >= 960 && keyVal <= 980)  {
          tone(8, notes[2]); // mi
          } // end else if
        
        else if(keyVal >= 900 && keyVal <= 945)  {
          tone(8, notes[3]); // fa
          } // end else if
        
        else if(keyVal >= 650 && keyVal <= 710)  {
          tone(8, notes[4]); // so
          } // end else if
        
        else if(keyVal >= 500 && keyVal <= 550)  {
          tone(8, notes[5]); //la
          } // end else if
        
        else if(keyVal >= 5 && keyVal <= 10)  {
          tone(8, notes[6]); // si
          } // end else if
        
        else if(keyVal <= 1)  { //se nao se carregar em nenhum butao nao faz som
          noTone(8);
          } // end else if

} //fim do loop do tom da frequência 

/////////////////////////////////////////////////////
void LCDstart()  {
  short keyVal = analogRead(A0);  
  LCDswitchState = digitalRead(LCDswitchPin); // ve se o buttao para menu foi carregado
  lcd.backlight();
    while (LCDswitchState == LOW)  { // continue loop while menu button isn't pressed
      LCDswitchState = digitalRead(LCDswitchPin); // check state of menu button every time loop starts
      
      //************* START SONG 1 TITLE LOOP ********************
      if (LCDswitchState == HIGH)  { // if menu button is pressed, then...
        LCDswitchCounter++; // set button count to 1
        Serial.print("butao carregado:  ");
        Serial.println(LCDswitchCounter);
        delay(300); // min. time until counts adds 1 more

        Song1title();
        lcd.clear();
        break;
        }

      //************* ELSE SHOW MENU ****************
      else   {  // if menu button is not pressed, then...
        LCDswitchCounter=0; // set menu button count to 0
        lcd.clear();
        lcd.setCursor(0, 0);
        lcd.print(" Selecione uma");
        lcd.setCursor(0, 1);
        lcd.print("musica p/ tocar");
        delay(50); // return to main 
        }
     
      } // end while
  } // end LCDstart loop
  
  
  

// ************* SONG 1 LOOP STARTS HERE **************  
void Song1title()  {
  short keyVal = analogRead(A0);
  LCDswitchState = digitalRead(LCDswitchPin); // check state of menu button again
  
  while (LCDswitchState == LOW)  { // continue loop while menu button isn't pressed  
    LCDswitchState = digitalRead(LCDswitchPin); // check state of menu button again 

      //************* START SONG 2 TITLE LOOP ********************
      if (LCDswitchState == HIGH)  { // if menu button is pressed, then...
        LCDswitchCounter++; // set button count to 2
        Serial.print("number of button pushes:  ");
        Serial.println(LCDswitchCounter);
        delay(300); // min. time until counts adds 1 more

        Song2title();
        lcd.clear();
        break;
        }
        
      else  { // if menu button is not pressed   
        short keyVal = analogRead(A0);
        Serial.println(keyVal); 
         
         if(keyVal >= 2)  {
           digitalWrite(LED, LOW);
           Song1();
           break;
           } // end if
        
        lcd.clear();
        lcd.setCursor(0, 0);
        lcd.print("SUPER MARIO BROS");
        lcd.setCursor(0, 1);
        lcd.print("   THEME SONG");
        delay(50);
        }
    } // end while song 1 -> 2
        
} // end Song1title loop




// ************* SONG 2 LOOP STARTS HERE **************  
void Song2title()  {
  short keyVal = analogRead(A0);
  LCDswitchState = digitalRead(LCDswitchPin); // check state of menu button again
  
  while (LCDswitchState == LOW)  { // continue loop while menu button isn't pressed  
    LCDswitchState = digitalRead(LCDswitchPin); // check state of menu button again 

      //************* START SONG 3 TITLE LOOP ********************
      if (LCDswitchState == HIGH)  { // if menu button is pressed, then...
        LCDswitchCounter++; // set button count to 3
        Serial.print("number of button pushes:  ");
        Serial.println(LCDswitchCounter);
        delay(300); // min. time until counts adds 1 more

        Song3title();
        lcd.clear();
        break;
        }
        
      else  { // if menu button is not pressed
        short keyVal = analogRead(A0);
        Serial.println(keyVal); 
         
         if(keyVal >= 2)  {
           digitalWrite(LED, LOW);
           Song2();
           break;
           } // end if
           
          lcd.clear();
          lcd.setCursor(0, 0);
          lcd.print("    StarWars");
          lcd.setCursor(0, 1);
          lcd.print(" Imperial March");
          delay(50);
          }
        
        } // end while song 2 -> 3
        
} // end Song2title loop




// ************* SONG 3 LOOP STARTS HERE **************  
void Song3title()  {
  short keyVal = analogRead(A0);
  LCDswitchState = digitalRead(LCDswitchPin); // check state of menu button again
  
  while (LCDswitchState == LOW)  { // continue loop while menu button isn't pressed  
    LCDswitchState = digitalRead(LCDswitchPin); // check state of menu button again 

      //************* START SONG 4 TITLE LOOP ********************
      if (LCDswitchState == HIGH)  { // if menu button is pressed, then...
        LCDswitchCounter++; // set button count to 4
        Serial.print("number of button pushes:  ");
        Serial.println(LCDswitchCounter);
        delay(300); // min. time until counts adds 1 more

        Song4title();
        lcd.clear();
        break;
        }
        
      else  { // if menu button is not pressed
        short keyVal = analogRead(A0);
        Serial.println(keyVal); 
         
         if(keyVal >= 2)  {
           digitalWrite(LED, LOW);
           Song3();
           break;
           } // end if
           
        lcd.clear();
        lcd.setCursor(0, 0);
        lcd.print("  Harry Potter");
        lcd.setCursor(0, 1);
        lcd.print("   THEME SONG");
        delay(50);
        }
        
        } // end while song 3 -> 4
        
} // end Song3title loop





// ************* SONG 4 LOOP STARTS HERE **************  
void Song4title()  {
  short keyVal = analogRead(A0);
  LCDswitchState = digitalRead(LCDswitchPin); // check state of menu button again
  
  while (LCDswitchState == LOW)  { // continue loop while menu button isn't pressed  
    LCDswitchState = digitalRead(LCDswitchPin); // check state of menu button again 

      //************* START SONG 5 TITLE LOOP ********************
      if (LCDswitchState == HIGH)  { // if menu button is pressed, then...
        LCDswitchCounter++; // set button count to 5
        Serial.print("number of button pushes:  ");
        Serial.println(LCDswitchCounter);
        delay(300); // min. time until counts adds 1 more

        Song5title();
        lcd.clear();
        break;
        }
        
      else  { // if menu button is not pressed
        short keyVal = analogRead(A0);
        Serial.println(keyVal); 
         
         if(keyVal >= 2)  {
           digitalWrite(LED, LOW);
           Song4();
           break;
           } // end if
          
          lcd.clear();
          lcd.setCursor(0, 0);
          lcd.print("Game of Thrones");
          lcd.setCursor(0, 1);
          lcd.print("     Opening");
          delay(50);
          }
        
        } // end while song 4 -> 5
        
} // end Song4title loop




// ************* SONG 5 LOOP STARTS HERE **************  
void Song5title()  {
  short keyVal = analogRead(A0);
  LCDswitchState = digitalRead(LCDswitchPin); // check state of menu button again
  
  while (LCDswitchState == LOW)  { // continue loop while menu button isn't pressed  
    LCDswitchState = digitalRead(LCDswitchPin); // check state of menu button again 

      //************* START SONG 5 TITLE LOOP ********************
      if (LCDswitchState == HIGH)  { // if menu button is pressed, then...
        LCDswitchCounter=0; // set button count to 0
        lcd.noBacklight();
        Serial.print("number of button pushes:  ");
        Serial.println(LCDswitchCounter);
        delay(300); // min. time until counts adds 1 more
        lcd.clear();
        }
        
      else  { // if menu button is not pressed
        short keyVal = analogRead(A0);
        Serial.println(keyVal); 
         
         if(keyVal >= 2)  {
           digitalWrite(LED, LOW);
           Song5();
           break;
           } // end if
           
          lcd.clear();
          lcd.setCursor(0, 0);
          lcd.print("     Darude");
          lcd.setCursor(0, 1);
          lcd.print("   Sandstrom");
          delay(50);
          }
        
        } // end while song 5 -> 6
        
} // end Song5title loop


void beep(short note, short duration)//starwars
{
  //Play tone on 8
  tone(8, note, duration);
 
  //Play different LED depending on value of 'counter'
  if(counter % 2 == 0)
  {
    digitalWrite(6, HIGH);
    delay(duration);
    digitalWrite(6, LOW);
  }else
  {
    digitalWrite(6, HIGH);
    delay(duration);
    digitalWrite(6, LOW);
  }
 
  //Stop tone on 8
  noTone(8);
 
  delay(50);
 
  //Increment counter
  counter++;
}
